# Fritzing sketch schema_panneau (saved by Fritzing 0.8.0b)
breadboards: 1

parts:
  LED1 = RGB LED (com. anode, rbg) [package="5 mm [THT]"]
  Composants1 = Arduino Board Ethernet
  R1 = Resistor [tolerance=±5% resistance=15 package=THT]
  R3 = Resistor [tolerance=±5% resistance=47 package=THT]
  R4 = Resistor [tolerance=±5% resistance=47 package=THT]
  R5 = Resistor [tolerance=±5% resistance=10 package=THT]
  R6 = Resistor [tolerance=±5% resistance=220 package=THT]
  R7 = Resistor [tolerance=±5% resistance=220 package=THT]
  LED2 = LED - 5mm [color="White (8000K)" package="5 mm [THT]"]
  R8 = Resistor [tolerance=±5% resistance=220 package=THT]
  J1 = Peltier Element  # not connected
  J2 = Peltier Element  # not connected

nets:
  N1: LED1.red_cathode, R5.Pin_1
  N2: LED1.common_anode, Composants1.GND, LED2.cathode
  N3: LED1.blue_cathode, R3.Pin_1
  N4: LED1.green_cathode, R4.Pin_1
  N5: Composants1.A0, R1.Pin_0
  N6: Composants1.A1, R6.Pin_0
  N7: Composants1.A2, R7.Pin_0
  N8: Composants1.A3, R8.Pin_0
  N9: LED2.anode, R8.Pin_1
